// Logisim project calc.circ as structural Verilog: 16 circuits, main circuit main
module main (
  input  in_1,
  input  in_2,
  input  in_3,
  input  in_4,
  input  in_5,
  input  in_6,
  input  in_7,
  input  in_8,
  input  in_9,
  input  in_10,
  input  in_11,
  input  in_12,
  input  in_13,
  input  in_14,
  input  in_15,
  input  in_16,
  output [3:0] out_17,
  output [3:0] out_18
);

  wire [3:0] calculator_1_r4;

  Hex_Digit_Display hex_digit_display_1 (.value(out_17));  // open: dp
  Hex_Digit_Display hex_digit_display_2 (.value(out_18));  // open: dp
  decoder decode (
    .a(in_1), .b(in_3), .c(in_5), .d(in_7), .e(in_6), .f(in_2), .g(in_4), .a1(out_17[3]), .a2(out_17[2]),
    .a3(out_17[1]), .a4(out_17[0]));
  decoder decode_2 (
    .a(in_10), .b(in_12), .c(in_14), .d(in_16), .e(in_15), .f(in_11), .g(in_13), .a1(out_18[3]),
    .a2(out_18[2]), .a3(out_18[1]), .a4(out_18[0]));
  Hex_Digit_Display hex_digit_display_3 (.value(calculator_1_r4));  // open: dp
  calculator calculator_1 (
    .a1(out_17[0]), .a2(out_17[1]), .a3(out_17[2]), .a4(out_17[3]), .b1(out_18[0]), .b2(out_18[1]),
    .b3(out_18[2]), .b4(out_18[3]), .in_9(in_8), .in_10(in_9), .r1(calculator_1_r4[3]),
    .r2(calculator_1_r4[2]), .r3(calculator_1_r4[1]), .r4(calculator_1_r4[0]));
endmodule

module calculator (
  input  a1,
  input  a2,
  input  a3,
  input  a4,
  input  b1,
  input  b2,
  input  b3,
  input  b4,
  input  in_9,
  input  in_10,
  output r1,
  output r2,
  output r3,
  output r4
);

  wire [3:0] \divisão_1_out_3 , \multiplicação_1_out_3 , somador_1_r1, \subtração_1_r1 ;

  somador somador_1 (
    .a1(a1), .b1(b1), .a2(a2), .b2(b2), .a3(a3), .b3(b3), .a4(a4), .b4(b4), .r1(somador_1_r1[0]),
    .r2(somador_1_r1[1]), .r3(somador_1_r1[2]), .r4(somador_1_r1[3]));  // open: cout
  \subtração  \subtração_1  (
    .a1(a1), .b1(b1), .a2(a2), .b2(b2), .a3(a3), .b3(b3), .a4(a4), .b4(b4), .r1(\subtração_1_r1 [0]),
    .r2(\subtração_1_r1 [1]), .r3(\subtração_1_r1 [2]), .r4(\subtração_1_r1 [3]));
  \multiplicação  \multiplicação_1  (
    .in_1({a4, a3, a2, a1}), .vezes({b4, b3, b2, b1}), .out_3(\multiplicação_1_out_3 ));
  \divisão  \divisão_1  (.Dividendo({a4, a3, a2, a1}), .Divisor({b4, b3, b2, b1}), .out_3(\divisão_1_out_3 ));
  mux_4_in mux_4_in_1 (
    ._00(somador_1_r1), ._01(\subtração_1_r1 ), ._10(\multiplicação_1_out_3 ), ._11(\divisão_1_out_3 ),
    .in_5(in_9), .in_6(in_10), .out_7({r1, r2, r3, r4}));
endmodule

module decoder (
  input  a,
  input  b,
  input  c,
  input  d,
  input  e,
  input  f,
  input  g,
  output a1,
  output a2,
  output a3,
  output a4
);

  wire and_1_out, and_2_out, and_3_out, and_4_out, and_5_out, and_6_out, and_7_out, and_8_out, and_9_out,
       and_10_out, and_11_out, and_12_out, and_13_out, and_14_out, and_15_out, not_1_out, not_2_out,
       not_3_out, not_4_out, not_5_out, not_6_out, not_7_out, not_8_out, not_9_out, not_10_out, not_11_out,
       not_12_out, not_13_out, not_14_out, not_15_out, not_16_out, not_17_out, not_18_out, not_19_out,
       not_20_out;

  not not_1 (not_1_out, a);
  not not_2 (not_2_out, b);
  not not_3 (not_3_out, b);
  not not_4 (not_4_out, c);
  not not_5 (not_5_out, e);
  not not_6 (not_6_out, a);
  not not_7 (not_7_out, b);
  not not_8 (not_8_out, d);
  not not_9 (not_9_out, e);
  not not_10 (not_10_out, b);
  not not_11 (not_11_out, d);
  not not_12 (not_12_out, f);
  not not_13 (not_13_out, b);
  not not_14 (not_14_out, a);
  not not_15 (not_15_out, b);
  not not_16 (not_16_out, a);
  not not_17 (not_17_out, f);
  not not_18 (not_18_out, c);
  not not_19 (not_19_out, d);
  not not_20 (not_20_out, e);
  and and_1 (and_1_out, not_1_out, not_2_out);
  and and_2 (and_2_out, not_3_out, not_4_out);
  and and_3 (and_3_out, b, c, e, g);
  and and_4 (and_4_out, a, b, not_5_out, f);
  and and_5 (and_5_out, not_6_out, b, g);
  and and_6 (and_6_out, a, not_7_out);
  and and_7 (and_7_out, a, not_8_out, not_9_out);
  and and_8 (and_8_out, not_10_out, c, e);
  and and_9 (and_9_out, a, not_11_out);
  and and_10 (and_10_out, a, not_12_out);
  and and_11 (and_11_out, a, not_13_out, e, g);
  and and_12 (and_12_out, not_14_out, not_15_out);
  and and_13 (and_13_out, not_16_out, not_17_out);
  and and_14 (and_14_out, not_18_out, not_19_out);
  and and_15 (and_15_out, a, not_20_out);
  or or_1 (a1, and_1_out, and_2_out, and_3_out, and_4_out);
  or or_2 (a2, and_5_out, and_6_out, and_7_out);
  or or_3 (a3, and_8_out, and_9_out, and_10_out, and_11_out);
  or or_4 (a4, and_12_out, and_13_out, and_14_out, and_15_out);
endmodule

module somador (
  input  a1,
  input  b1,
  input  a2,
  input  b2,
  input  a3,
  input  b3,
  input  a4,
  input  b4,
  output r1,
  output r2,
  output r3,
  output r4,
  output cout
);

  wire soma_bit1_carryout, soma_bit2_carryout, soma_bit3_carryout;

  somabit soma_bit1 (.a1(a1), .a2(b1), .cin(1'b0), .soma(r1), .carryout(soma_bit1_carryout));
  somabit soma_bit2 (.a1(a2), .a2(b2), .cin(soma_bit1_carryout), .soma(r2), .carryout(soma_bit2_carryout));
  somabit soma_bit3 (.a1(a3), .a2(b3), .cin(soma_bit2_carryout), .soma(r3), .carryout(soma_bit3_carryout));
  somabit soma_bit4 (.a1(a4), .a2(b4), .cin(soma_bit3_carryout), .soma(r4), .carryout(cout));
endmodule

module somador_4bits_1_in (
  input  [3:0] in_1,
  input  [3:0] in_2,
  output [3:0] out_3
);

  somador somador_1 (
    .a1(in_1[0]), .b1(in_2[0]), .a2(in_1[1]), .b2(in_2[1]), .a3(in_1[2]), .b3(in_2[2]), .a4(in_1[3]),
    .b4(in_2[3]), .r1(out_3[0]), .r2(out_3[1]), .r3(out_3[2]), .r4(out_3[3]));  // open: cout
endmodule

module somabit (
  input  a1,
  input  a2,
  input  cin,
  output soma,
  output carryout
);

  wire and_1_out, and_2_out, and_3_out, and_4_out, and_5_out, and_6_out, and_7_out, not_1_out, not_2_out,
       not_3_out, not_4_out, not_5_out, not_6_out;

  not not_1 (not_1_out, a1);
  not not_2 (not_2_out, a2);
  not not_3 (not_3_out, a1);
  not not_4 (not_4_out, cin);
  not not_5 (not_5_out, a2);
  not not_6 (not_6_out, cin);
  and and_1 (and_1_out, a2, cin);
  and and_2 (and_2_out, a1, cin);
  and and_3 (and_3_out, a1, a2);
  and and_4 (and_4_out, not_1_out, not_2_out, cin);
  and and_5 (and_5_out, not_3_out, a2, not_4_out);
  and and_6 (and_6_out, a1, not_5_out, not_6_out);
  and and_7 (and_7_out, a1, a2, cin);
  or or_1 (carryout, and_1_out, and_2_out, and_3_out);
  or or_2 (soma, and_4_out, and_5_out, and_6_out, and_7_out);
endmodule

module subtraibit (
  input  a1,
  input  b1,
  input  emprest,
  output \diferença ,
  output proximasub
);

  wire and_1_out, and_2_out, and_3_out, and_4_out, and_5_out, and_6_out, and_7_out, not_1_out, not_2_out,
       not_3_out, not_4_out, not_5_out, not_6_out, not_7_out, not_8_out;

  not not_1 (not_1_out, a1);
  not not_2 (not_2_out, b1);
  not not_3 (not_3_out, a1);
  not not_4 (not_4_out, emprest);
  not not_5 (not_5_out, b1);
  not not_6 (not_6_out, emprest);
  not not_7 (not_7_out, a1);
  not not_8 (not_8_out, a1);
  and and_1 (and_1_out, not_1_out, not_2_out, emprest);
  and and_2 (and_2_out, not_3_out, b1, not_4_out);
  and and_3 (and_3_out, a1, not_5_out, not_6_out);
  and and_4 (and_4_out, a1, b1, emprest);
  and and_5 (and_5_out, not_7_out, emprest);
  and and_6 (and_6_out, not_8_out, b1);
  and and_7 (and_7_out, b1, emprest);
  or or_1 (\diferença , and_1_out, and_2_out, and_3_out, and_4_out);
  or or_2 (proximasub, and_5_out, and_6_out, and_7_out);
endmodule

module \subtração  (
  input  a1,
  input  b1,
  input  a2,
  input  b2,
  input  a3,
  input  b3,
  input  a4,
  input  b4,
  output r1,
  output r2,
  output r3,
  output r4
);

  wire subtraibit_1_proximasub, subtraibit_2_proximasub, subtraibit_3_proximasub;

  subtraibit subtraibit_1 (.a1(a1), .b1(b1), .emprest(1'b0), .\diferença (r1), .proximasub(subtraibit_1_proximasub));
  subtraibit subtraibit_2 (
    .a1(a2), .b1(b2), .emprest(subtraibit_1_proximasub), .\diferença (r2),
    .proximasub(subtraibit_2_proximasub));
  subtraibit subtraibit_3 (
    .a1(a3), .b1(b3), .emprest(subtraibit_2_proximasub), .\diferença (r3),
    .proximasub(subtraibit_3_proximasub));
  subtraibit subtraibit_4 (.a1(a4), .b1(b4), .emprest(subtraibit_3_proximasub), .\diferença (r4));  // open: proximasub
endmodule

module \subtração_4bits_1_in  (
  input  [3:0] in_1,
  input  [3:0] in_2,
  output [3:0] out_3
);

  \subtração  \subtração_1  (
    .a1(in_1[0]), .b1(in_2[0]), .a2(in_1[1]), .b2(in_2[1]), .a3(in_1[2]), .b3(in_2[2]), .a4(in_1[3]),
    .b4(in_2[3]), .r1(out_3[0]), .r2(out_3[1]), .r3(out_3[2]), .r4(out_3[3]));
endmodule

module \multiplicação  (
  input  [3:0] in_1,
  input  [3:0] vezes,
  output [3:0] out_3
);

  wire and_1_out, not_1_out, not_2_out, not_3_out, not_4_out, somador_1_r1, somador_1_r2, somador_1_r3,
       somador_1_r4, somador_2_r1, somador_2_r2, somador_2_r3, somador_2_r4;
  wire [3:0] mux_1_out_4, mux_2_out_4, mux_3_out_4, mux_4_out_4, somador_3_r1;

  mux mux_1 (.in_1(in_1), .in_2(4'b0000), .in_3(not_1_out), .out_4(mux_1_out_4));
  not not_1 (not_1_out, vezes[0]);
  mux mux_2 (.in_1(in_1), .in_2(4'b0000), .in_3(not_2_out), .out_4(mux_2_out_4));
  not not_2 (not_2_out, vezes[1]);
  mux mux_3 (.in_1(in_1), .in_2(4'b0000), .in_3(not_3_out), .out_4(mux_3_out_4));
  not not_3 (not_3_out, vezes[2]);
  somador somador_1 (
    .a1(mux_1_out_4[0]), .b1(1'b0), .a2(mux_1_out_4[1]), .b2(mux_2_out_4[0]), .a3(mux_1_out_4[2]),
    .b3(mux_2_out_4[1]), .a4(mux_1_out_4[3]), .b4(mux_2_out_4[2]), .r1(somador_1_r1), .r2(somador_1_r2),
    .r3(somador_1_r3), .r4(somador_1_r4));  // open: cout
  mux mux_4 (.in_1(in_1), .in_2(4'b0000), .in_3(not_4_out), .out_4(mux_4_out_4));
  not not_4 (not_4_out, vezes[3]);
  somador somador_2 (
    .a1(somador_1_r1), .b1(1'b0), .a2(somador_1_r2), .b2(1'b0), .a3(somador_1_r3), .b3(mux_3_out_4[0]),
    .a4(somador_1_r4), .b4(mux_3_out_4[1]), .r1(somador_2_r1), .r2(somador_2_r2), .r3(somador_2_r3),
    .r4(somador_2_r4));  // open: cout
  and and_1 (and_1_out, ~vezes[3], ~vezes[2], ~vezes[1], ~vezes[0]);  // AND_Gate
  somador somador_3 (
    .a1(somador_2_r1), .b1(1'b0), .a2(somador_2_r2), .b2(1'b0), .a3(somador_2_r3), .b3(1'b0),
    .a4(somador_2_r4), .b4(mux_4_out_4[0]), .r1(somador_3_r1[0]), .r2(somador_3_r1[1]), .r3(somador_3_r1[2]),
    .r4(somador_3_r1[3]));  // open: cout
  mux mux_5 (.in_1(somador_3_r1), .in_2(4'b0000), .in_3(and_1_out), .out_4(out_3));

  // Notes on the sheet:
  //   Se mul = 0
endmodule

module \divisão  (
  input  [3:0] Dividendo,
  input  [3:0] Divisor,
  output [3:0] out_3
);

  wire mag_1_out_3, mag_2_out_3, mag_3_out_3, mag_4_out_3, mag_5_out_3, mag_6_out_3, mag_7_out_3,
       mag_8_out_3, mag_9_out_3, mag_10_out_3, mag_11_out_3, mag_12_out_3, mag_13_out_3, mag_14_out_3,
       mag_15_out_3, soma_perm_1_out_5, soma_perm_2_out_5, soma_perm_3_out_5, soma_perm_4_out_5,
       soma_perm_5_out_5, soma_perm_6_out_5, soma_perm_7_out_5, soma_perm_8_out_5, soma_perm_9_out_5,
       soma_perm_10_out_5, soma_perm_11_out_5, soma_perm_12_out_5, soma_perm_13_out_5;
  wire [3:0] incrementador_1_out_3, incrementador_2_out_3, incrementador_3_out_3, incrementador_4_out_3,
       incrementador_5_out_3, incrementador_6_out_3, incrementador_7_out_3, incrementador_8_out_3,
       incrementador_9_out_3, incrementador_10_out_3, incrementador_11_out_3, incrementador_12_out_3,
       incrementador_13_out_3, incrementador_14_out_3, \multiplicação_1_out_3 , \multiplicação_2_out_3 ,
       \multiplicação_3_out_3 , \multiplicação_4_out_3 , \multiplicação_5_out_3 , \multiplicação_6_out_3 ,
       \multiplicação_7_out_3 , \multiplicação_8_out_3 , \multiplicação_9_out_3 , \multiplicação_10_out_3 ,
       \multiplicação_11_out_3 , \multiplicação_12_out_3 , \multiplicação_13_out_3 ,
       \multiplicação_14_out_3 , soma_perm_1_out_6, soma_perm_2_out_6, soma_perm_3_out_6, soma_perm_4_out_6,
       soma_perm_5_out_6, soma_perm_6_out_6, soma_perm_7_out_6, soma_perm_8_out_6, soma_perm_9_out_6,
       soma_perm_10_out_6, soma_perm_11_out_6, soma_perm_12_out_6, soma_perm_13_out_6, soma_perm_14_out_6;

  Hex_Digit_Display hex_digit_display_1 (.value(Dividendo));  // open: dp
  incrementador incrementador_1 (.in_1(4'b0001), .perm(1'b0), .out_3(incrementador_1_out_3));
  Hex_Digit_Display hex_digit_display_2 (.value(Divisor));  // open: dp
  mag mag_1 (.in_1(Dividendo), .in_2(\multiplicação_1_out_3 ), .out_3(mag_1_out_3));  // open: out_4, out_5
  \multiplicação  \multiplicação_1  (.in_1(incrementador_1_out_3), .vezes(Divisor), .out_3(\multiplicação_1_out_3 ));
  incrementador incrementador_2 (.in_1(incrementador_1_out_3), .perm(1'b0), .out_3(incrementador_2_out_3));
  soma_perm soma_perm_1 (
    .in_1(incrementador_1_out_3), .in_2(4'b0000), .som(1'b0), .out_5(soma_perm_1_out_5), .in_4(mag_1_out_3),
    .out_6(soma_perm_1_out_6));
  mag mag_2 (.in_1(Dividendo), .in_2(\multiplicação_2_out_3 ), .out_3(mag_2_out_3));  // open: out_4, out_5
  \multiplicação  \multiplicação_2  (.in_1(incrementador_2_out_3), .vezes(Divisor), .out_3(\multiplicação_2_out_3 ));
  incrementador incrementador_3 (.in_1(incrementador_2_out_3), .perm(1'b0), .out_3(incrementador_3_out_3));
  soma_perm soma_perm_2 (
    .in_1(incrementador_2_out_3), .in_2(soma_perm_1_out_6), .som(soma_perm_1_out_5),
    .out_5(soma_perm_2_out_5), .in_4(mag_2_out_3), .out_6(soma_perm_2_out_6));
  mag mag_3 (.in_1(Dividendo), .in_2(\multiplicação_3_out_3 ), .out_3(mag_3_out_3));  // open: out_4, out_5
  \multiplicação  \multiplicação_3  (.in_1(incrementador_3_out_3), .vezes(Divisor), .out_3(\multiplicação_3_out_3 ));
  incrementador incrementador_4 (.in_1(incrementador_3_out_3), .perm(1'b0), .out_3(incrementador_4_out_3));
  soma_perm soma_perm_3 (
    .in_1(incrementador_3_out_3), .in_2(soma_perm_2_out_6), .som(soma_perm_2_out_5),
    .out_5(soma_perm_3_out_5), .in_4(mag_3_out_3), .out_6(soma_perm_3_out_6));
  mag mag_4 (.in_1(Dividendo), .in_2(\multiplicação_4_out_3 ), .out_3(mag_4_out_3));  // open: out_4, out_5
  \multiplicação  \multiplicação_4  (.in_1(incrementador_4_out_3), .vezes(Divisor), .out_3(\multiplicação_4_out_3 ));
  incrementador incrementador_5 (.in_1(incrementador_4_out_3), .perm(1'b0), .out_3(incrementador_5_out_3));
  soma_perm soma_perm_4 (
    .in_1(incrementador_4_out_3), .in_2(soma_perm_3_out_6), .som(soma_perm_3_out_5),
    .out_5(soma_perm_4_out_5), .in_4(mag_4_out_3), .out_6(soma_perm_4_out_6));
  mag mag_5 (.in_1(Dividendo), .in_2(\multiplicação_5_out_3 ), .out_3(mag_5_out_3));  // open: out_4, out_5
  \multiplicação  \multiplicação_5  (.in_1(incrementador_5_out_3), .vezes(Divisor), .out_3(\multiplicação_5_out_3 ));
  incrementador incrementador_6 (.in_1(incrementador_5_out_3), .perm(1'b0), .out_3(incrementador_6_out_3));
  soma_perm soma_perm_5 (
    .in_1(incrementador_5_out_3), .in_2(soma_perm_4_out_6), .som(soma_perm_4_out_5),
    .out_5(soma_perm_5_out_5), .in_4(mag_5_out_3), .out_6(soma_perm_5_out_6));
  mag mag_6 (.in_1(Dividendo), .in_2(\multiplicação_6_out_3 ), .out_3(mag_6_out_3));  // open: out_4, out_5
  \multiplicação  \multiplicação_6  (.in_1(incrementador_6_out_3), .vezes(Divisor), .out_3(\multiplicação_6_out_3 ));
  incrementador incrementador_7 (.in_1(incrementador_6_out_3), .perm(1'b0), .out_3(incrementador_7_out_3));
  soma_perm soma_perm_6 (
    .in_1(incrementador_6_out_3), .in_2(soma_perm_5_out_6), .som(soma_perm_5_out_5),
    .out_5(soma_perm_6_out_5), .in_4(mag_6_out_3), .out_6(soma_perm_6_out_6));
  mag mag_7 (.in_1(Dividendo), .in_2(\multiplicação_7_out_3 ), .out_3(mag_7_out_3));  // open: out_4, out_5
  \multiplicação  \multiplicação_7  (.in_1(incrementador_7_out_3), .vezes(Divisor), .out_3(\multiplicação_7_out_3 ));
  incrementador incrementador_8 (.in_1(incrementador_7_out_3), .perm(1'b0), .out_3(incrementador_8_out_3));
  soma_perm soma_perm_7 (
    .in_1(incrementador_7_out_3), .in_2(soma_perm_6_out_6), .som(soma_perm_6_out_5),
    .out_5(soma_perm_7_out_5), .in_4(mag_7_out_3), .out_6(soma_perm_7_out_6));
  mag mag_8 (.in_1(Dividendo), .in_2(\multiplicação_8_out_3 ), .out_3(mag_8_out_3));  // open: out_4, out_5
  \multiplicação  \multiplicação_8  (.in_1(incrementador_8_out_3), .vezes(Divisor), .out_3(\multiplicação_8_out_3 ));
  incrementador incrementador_9 (.in_1(incrementador_8_out_3), .perm(1'b0), .out_3(incrementador_9_out_3));
  soma_perm soma_perm_8 (
    .in_1(incrementador_8_out_3), .in_2(soma_perm_7_out_6), .som(soma_perm_7_out_5),
    .out_5(soma_perm_8_out_5), .in_4(mag_8_out_3), .out_6(soma_perm_8_out_6));
  mag mag_9 (.in_1(Dividendo), .in_2(\multiplicação_9_out_3 ), .out_3(mag_9_out_3));  // open: out_4, out_5
  \multiplicação  \multiplicação_9  (.in_1(incrementador_9_out_3), .vezes(Divisor), .out_3(\multiplicação_9_out_3 ));
  incrementador incrementador_10 (.in_1(incrementador_9_out_3), .perm(1'b0), .out_3(incrementador_10_out_3));
  soma_perm soma_perm_9 (
    .in_1(incrementador_9_out_3), .in_2(soma_perm_8_out_6), .som(soma_perm_8_out_5),
    .out_5(soma_perm_9_out_5), .in_4(mag_9_out_3), .out_6(soma_perm_9_out_6));
  mag mag_10 (.in_1(Dividendo), .in_2(\multiplicação_10_out_3 ), .out_3(mag_10_out_3));  // open: out_4, out_5
  \multiplicação  \multiplicação_10  (.in_1(incrementador_10_out_3), .vezes(Divisor), .out_3(\multiplicação_10_out_3 ));
  incrementador incrementador_11 (.in_1(incrementador_10_out_3), .perm(1'b0), .out_3(incrementador_11_out_3));
  soma_perm soma_perm_10 (
    .in_1(incrementador_10_out_3), .in_2(soma_perm_9_out_6), .som(soma_perm_9_out_5),
    .out_5(soma_perm_10_out_5), .in_4(mag_10_out_3), .out_6(soma_perm_10_out_6));
  mag mag_11 (.in_1(Dividendo), .in_2(\multiplicação_11_out_3 ), .out_3(mag_11_out_3));  // open: out_4, out_5
  \multiplicação  \multiplicação_11  (.in_1(incrementador_11_out_3), .vezes(Divisor), .out_3(\multiplicação_11_out_3 ));
  incrementador incrementador_12 (.in_1(incrementador_11_out_3), .perm(1'b0), .out_3(incrementador_12_out_3));
  soma_perm soma_perm_11 (
    .in_1(incrementador_11_out_3), .in_2(soma_perm_10_out_6), .som(soma_perm_10_out_5),
    .out_5(soma_perm_11_out_5), .in_4(mag_11_out_3), .out_6(soma_perm_11_out_6));
  mag mag_12 (.in_1(Dividendo), .in_2(\multiplicação_12_out_3 ), .out_3(mag_12_out_3));  // open: out_4, out_5
  \multiplicação  \multiplicação_12  (.in_1(incrementador_12_out_3), .vezes(Divisor), .out_3(\multiplicação_12_out_3 ));
  incrementador incrementador_13 (.in_1(incrementador_12_out_3), .perm(1'b0), .out_3(incrementador_13_out_3));
  soma_perm soma_perm_12 (
    .in_1(incrementador_12_out_3), .in_2(soma_perm_11_out_6), .som(soma_perm_11_out_5),
    .out_5(soma_perm_12_out_5), .in_4(mag_12_out_3), .out_6(soma_perm_12_out_6));
  mag mag_13 (.in_1(Dividendo), .in_2(\multiplicação_13_out_3 ), .out_3(mag_13_out_3));  // open: out_4, out_5
  \multiplicação  \multiplicação_13  (.in_1(incrementador_13_out_3), .vezes(Divisor), .out_3(\multiplicação_13_out_3 ));
  incrementador incrementador_14 (.in_1(incrementador_13_out_3), .perm(1'b0), .out_3(incrementador_14_out_3));
  soma_perm soma_perm_13 (
    .in_1(incrementador_13_out_3), .in_2(soma_perm_12_out_6), .som(soma_perm_12_out_5),
    .out_5(soma_perm_13_out_5), .in_4(mag_13_out_3), .out_6(soma_perm_13_out_6));
  mag mag_14 (.in_1(Dividendo), .in_2(\multiplicação_14_out_3 ), .out_3(mag_14_out_3));  // open: out_4, out_5
  \multiplicação  \multiplicação_14  (.in_1(incrementador_14_out_3), .vezes(Divisor), .out_3(\multiplicação_14_out_3 ));
  mag mag_15 (.in_1(Dividendo), .in_2(Divisor), .out_3(mag_15_out_3));  // open: out_4, out_5
  soma_perm soma_perm_14 (
    .in_1(incrementador_14_out_3), .in_2(soma_perm_13_out_6), .som(soma_perm_13_out_5), .in_4(mag_14_out_3),
    .out_6(soma_perm_14_out_6));  // open: out_5
  Hex_Digit_Display hex_digit_display_3 (.value(out_3));  // open: dp
  mux mux_1 (.in_1(soma_perm_14_out_6), .in_2(4'b0001), .in_3(mag_15_out_3), .out_4(out_3));
endmodule

module mux (
  input  [3:0] in_1,
  input  [3:0] in_2,
  input  in_3,
  output [3:0] out_4
);

  wire [3:0] and_1_out, and_2_out;

  assign and_1_out = in_1 & ~{4{in_3}};  // AND_Gate and_1, 4 bits wide
  assign and_2_out = in_2 & {4{in_3}};  // AND_Gate and_2, 4 bits wide
  assign out_4 = and_1_out | and_2_out;  // OR_Gate or_1, 4 bits wide
endmodule

module mux_4_in (
  input  [3:0] _00,
  input  [3:0] _01,
  input  [3:0] _10,
  input  [3:0] _11,
  input  in_5,
  input  in_6,
  output [3:0] out_7
);

  wire and_1_out;
  wire [3:0] mux_1_out_4, mux_2_out_4;

  mux mux_1 (.in_1(_00), .in_2(_10), .in_3(in_5), .out_4(mux_1_out_4));
  mux mux_2 (.in_1(mux_1_out_4), .in_2(_01), .in_3(in_6), .out_4(mux_2_out_4));
  mux mux_3 (.in_1(mux_2_out_4), .in_2(_11), .in_3(and_1_out), .out_4(out_7));
  and and_1 (and_1_out, in_5, in_6);
endmodule

module mag (
  input  [3:0] in_1,
  input  [3:0] in_2,
  output out_3,
  output out_4,
  output out_5
);

  wire _0_out, _1_out, _2_out, _3_out, and_2_out, and_3_out, and_4_out, and_5_out;

  xnor _0 (_0_out, in_1[0], in_2[0]);
  xnor _1 (_1_out, in_1[1], in_2[1]);
  xnor _2 (_2_out, in_2[2], in_1[2]);
  xnor _3 (_3_out, in_1[3], in_2[3]);
  and \and  (out_3, _0_out, _1_out, _2_out, _3_out);
  and and_2 (and_2_out, in_1[3], ~in_2[3]);  // AND_Gate
  and and_3 (and_3_out, _3_out, in_1[2], ~in_2[2]);  // AND_Gate
  and and_4 (and_4_out, _3_out, _2_out, in_1[1], ~in_2[1]);  // AND_Gate
  and and_5 (and_5_out, _3_out, _2_out, _1_out, in_1[0], ~in_2[0]);  // AND_Gate
  or \or  (out_4, and_2_out, and_3_out, and_4_out, and_5_out);
  and and_6 (out_5, ~out_3, ~out_4);  // AND_Gate
endmodule

module incrementador (
  input  [3:0] in_1,
  input  perm,
  output [3:0] out_3
);

  wire [3:0] and_1_out;

  assign and_1_out = 4'b0001 & ~{4{perm}};  // AND_Gate and_1, 4 bits wide
  somador somador_1 (
    .a1(in_1[0]), .b1(and_1_out[0]), .a2(in_1[1]), .b2(and_1_out[1]), .a3(in_1[2]), .b3(and_1_out[2]),
    .a4(in_1[3]), .b4(and_1_out[3]), .r1(out_3[0]), .r2(out_3[1]), .r3(out_3[2]), .r4(out_3[3]));  // open: cout
endmodule

module soma_perm (
  input  [3:0] in_1,
  input  [3:0] in_2,
  input  som,
  input  in_4,
  output out_5,
  output [3:0] out_6
);

  wire and_1_out, not_1_out;
  wire [3:0] mux_1_out_4;

  mux mux_1 (.in_1(in_1), .in_2(4'b0000), .in_3(not_1_out), .out_4(mux_1_out_4));
  not not_1 (not_1_out, and_1_out);
  and and_1 (and_1_out, ~som, in_4);  // AND_Gate
  somador_4bits_1_in somador_4bits_1_in_1 (.in_1(mux_1_out_4), .in_2(in_2), .out_3(out_6));
  mag mag_1 (.in_1(out_6), .in_2(4'b0000), .out_4(out_5));  // open: out_3, out_5
endmodule
